# Fritzing sketch Yukari (saved by Fritzing 0.9.3b)
breadboards: 1

parts:
  U401 = Arduino Nano (Rev3.0)
  U201 = IC, SIP package, 4 pins [chip_label=MPU9250]
  J301 = male pin header, 3 pins [form="♂ (male)" part_number=Steering]
  J302 = male pin header, 4 pins [form="♂ (male)" part_number=Throttle]
  U301 = IC, DIP package, 8 pins [chip_label=IC]
  D301 = LED - 5mm [color="Green (560nm)" package="5 mm [THT]"]
  R301 = Resistor [tolerance=±5% resistance=220 package=THT]
  J501 = Adafruit GPS FeatherWing [part_number="Adafruit #3133"]
  S117 = SWITCH_SPDT [part_number="SPDT NO switch" package=kps-1290]
  J101 = Adafruit Pi Cobbler [part_number="26-pin Pi hookup"]
  R413 = Resistor [tolerance=±5% resistance=220 package=THT]
  D413 = LED - 5mm [color="Yellow (585nm)" package="5 mm [THT]"]
  R402 = Resistor [tolerance=±5% resistance=220 package=THT]
  D402 = LED - 5mm [color="Red (660nm)" package="5 mm [THT]"]
  J403 = male pin header, 3 pins [form="♂ (male)" part_number="Encoder 1"]
  J400 = male pin header, 3 pins [form="♂ (male)" part_number="Encoder 0"]
  D122 = smd LED [color="Red (660nm)" package="1206 [SMD]"]
  R122 = Resistor [tolerance=±5% resistance=220 package=THT]
  R117 = Resistor [tolerance=±5% resistance=10k package=THT]

nets:
  N1: U401.GND, U301.pin4, D413.cathode, J403.pin1, J400.pin3
  N2: U401.D2, R402.Pin_0
  N3: U401.D5, U301.pin3
  N4: U401.D6, U301.pin2
  N5: U401.5V, U301.pin1, J101.5.0V, J403.pin2, J400.pin2
  N6: U401.A5, U201.pin4, J101.SCL
  N7: U401.A4, U201.pin3, J101.SDA
  N8: U401.A3, J403.pin3
  N9: U401.A0, J400.pin1
  N10: U401.D13/SCK, R413.Pin_0
  GND: U201.pin1, J501.C, J501.GND, S117.P, J101.GND, D402.cathode, D122.cathode
  N11: U201.pin2, J501.D, J501.3V, J501.E, J101.3.3V, R117.Pin_0
  N12: J301.pin1, J302.pin1, U301.pin5, R301.Pin_1
  N13: J301.pin2, J302.pin2, U301.pin8, D301.anode
  N14: J301.pin3, U301.pin6
  N15: J302.pin3, U301.pin7
  N16: D301.cathode, R301.Pin_0
  N17: J501.1PPS, J501.F, J101.GPIO18
  N18: J501.GPS_RX, J501.A, J101.TXD
  N19: J501.GPS_TX, J501.B, J101.RXD
  N20: S117.S, J101.GPIO17, R117.Pin_1
  N21: J101.GPIO22, R122.Pin_1
  N22: R413.Pin_1, D413.anode
  N23: R402.Pin_1, D402.anode
  N24: D122.anode, R122.Pin_0

notes:
  D122 is PPS echo. It is software driven and indicates that the GPS is in lock, and that the Pi software is receiving the PPS.
  S117 is the Go button, hooked to a GPIO as input on the Pi. R117 is the pullup, so this signal is normally on, and only off when S117 shorts the red wire to ground.
  The GPS is a FeatherWing. In this case, there are 6 consecutive unused pins on the edge that can be wired to match the pinout of the UP501. It communicates via TTL serial and has a PPS output
  U201 is an MPU9250
  9-axis sensor, communicating on I2C
  U301 is an ADUM3221
  magnetic isolator. The bottom edge runs at Pi 5V, and the upper edge runs at motor voltage. Two servo command signals are bridged between voltages using this device.
  J101 is the 26-pin connector to a Raspberry Pi 1 model B
  D301 is the motor power indicator
  U401 is an Arduino Nano which handles
  "microcontroller" tasks that the Pi isn't good at - accurate timing of servo pulses and analog input
  D402 echoes the reading of encoder 0
  D413 echoes the reading of encoder 1

custom parts:
  Adafruit GPS FeatherWing: Give your Feather a sense of place, with an Ultimate GPS FeatherWing. In 2013 we designed the Ultimate GPS module to satisfy all your GPS desires - and now we have brought its power and versatility plus more to our Feather series with the Adafruit Ultimate GPS FeatherWing! This FeatherWing plugs right into your Feather board and gives it a precise, sensitive, and low power GPS module for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
  Adafruit Pi Cobbler: Now that you've finally got your hands on a Raspberry Pi® Model B , you're probably itching to make some fun embedded computer projects with it. What you need is an add on prototyping Pi Cobbler from Adafruit, which can break out all those tasty power, GPIO, I2C and SPI pins from the 26 pin header onto a solderless breadboard. This set will make "cobbling together" prototypes with the Pi super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
