# Fritzing sketch Common Emitter Phototransistor (saved by Fritzing 0.9.3b)

parts:
  R1 = Resistor [tolerance=±5% resistance=10k package=THT]
  Q1 = LTR-301 [package=ltr-301]
  OUT1 = female pin header, 1 pin [form="♀ (female)"]
  R2 = Resistor [tolerance=±5% resistance=10k package=THT]
  OUT2 = female pin header, 1 pin [form="♀ (female)"]
  Q3 = TRANSISTOR_NPN [package=to-92-ammo]
  IN = female pin header, 1 pin [form="♀ (female)"]

nets:
  5V: R1.Pin_1, R2.Pin_1
  N1: Q1.C, OUT1.pin1
  GND: Q1.E, Q3.E
  N2: R2.Pin_0, OUT2.pin1, Q3.C
  N3: Q3.B, IN.pin1
