# Fritzing sketch LED (saved by Fritzing 0.9.3b)

parts:
  R1 = Resistor [tolerance=±5% resistance=220 package=THT]
  LED1 = LED - 3mm [color="Infrared (940nm)" current=17.5mA package="3 mm [THT]"]

nets:
  N1: R1.Pin_0, LED1.anode
  5V: R1.Pin_1
  GND: LED1.cathode
